# Fritzing sketch pinbit_bme680 (saved by Fritzing 0.9.3b)
breadboards: 1

parts:
  B1 = pinbit micro:bit breakout [package="SIP (Single Inline) [THT]"]
  U1 = BME680 [chip_label=BME680 package="SIP (Single Inline) [THT]"]
  JACK1 = 2.1mm Barrel Jack with Terminal Block  # not connected

nets:
  N1: B1.pin19, U1.pin3
  N2: B1.pin20, U1.pin4
  N3: B1.3v, U1.pin1
  N4: B1.GND, U1.pin2

notes:
  USB POWER SOURCE

custom parts:
  pinbit micro:bit breakout: Pmoroni's pin:bit breakout board for micro:bit
  BME680: BME680 Generic Breeakout Module
