# Fritzing sketch BME680 (saved by Fritzing 0.9.3b)

parts:
  Raspberry_Pi_1 = Raspberry Pi 3 [part_number=RPI-3-V1.2]
  U1 = BME680 [chip_label=BME680 package="SIP (Single Inline) [THT]"]

nets:
  N1: Raspberry_Pi_1.3v3, U1.pin1
  N2: Raspberry_Pi_1.GPIO2, U1.pin4
  N3: Raspberry_Pi_1.GPIO3, U1.pin3
  N4: Raspberry_Pi_1.GND, U1.pin2

custom parts:
  BME680: BME680 Generic Breeakout Module
